// Logisim project AriesComputer.circ as structural Verilog
module RippleCarryAdder32Bit (
  input  Cin,
  input  [31:0] A,
  input  [31:0] B,
  output [31:0] S,
  output Cout
);

  wire ripplecarryadder16bit_1_cout;

  RippleCarryAdder16Bit ripplecarryadder16bit_1 (
    .Cin(Cin), .A(A[15:0]), .B(B[15:0]), .S(S[15:0]), .Cout(ripplecarryadder16bit_1_cout));
  RippleCarryAdder16Bit ripplecarryadder16bit_2 (
    .Cin(ripplecarryadder16bit_1_cout), .A(A[31:16]), .B(B[31:16]), .S(S[31:16]), .Cout(Cout));
endmodule

module RippleCarryAdder1Bit (
  input  A,
  input  B,
  input  Cin,
  output S,
  output Cout
);

  wire and_1_out, and_2_out, and_3_out, or_2_out, xor_1_out;

  xor xor_1 (xor_1_out, B, Cin);
  xor xor_2 (S, A, xor_1_out);
  and and_1 (and_1_out, Cin, B);
  or or_1 (Cout, and_1_out, or_2_out);
  and and_2 (and_2_out, Cin, A);
  and and_3 (and_3_out, B, A);
  or or_2 (or_2_out, and_2_out, and_3_out);
endmodule

module RippleCarryAdder4Bit (
  input  [3:0] A,
  input  [3:0] B,
  input  Cin,
  output [3:0] S,
  output Cout
);

  wire ripplecarryadder1bit_1_cout, ripplecarryadder1bit_2_cout, ripplecarryadder1bit_3_cout;

  RippleCarryAdder1Bit ripplecarryadder1bit_1 (
    .A(A[0]), .B(B[0]), .Cin(Cin), .S(S[0]), .Cout(ripplecarryadder1bit_1_cout));
  RippleCarryAdder1Bit ripplecarryadder1bit_2 (
    .A(A[1]), .B(B[1]), .Cin(ripplecarryadder1bit_1_cout), .S(S[1]), .Cout(ripplecarryadder1bit_2_cout));
  RippleCarryAdder1Bit ripplecarryadder1bit_3 (
    .A(A[2]), .B(B[2]), .Cin(ripplecarryadder1bit_2_cout), .S(S[2]), .Cout(ripplecarryadder1bit_3_cout));
  RippleCarryAdder1Bit ripplecarryadder1bit_4 (
    .A(A[3]), .B(B[3]), .Cin(ripplecarryadder1bit_3_cout), .S(S[3]), .Cout(Cout));
endmodule

module RippleCarryAdder16Bit (
  input  Cin,
  input  [15:0] A,
  input  [15:0] B,
  output [15:0] S,
  output Cout
);

  wire ripplecarryadder4bit_1_cout, ripplecarryadder4bit_2_cout, ripplecarryadder4bit_3_cout;

  // Probe on A[3:0]
  // Probe on A[7:4]
  // Probe on A[11:8]
  // Probe on A[15:12]
  RippleCarryAdder4Bit ripplecarryadder4bit_1 (
    .A(A[3:0]), .B(B[3:0]), .Cin(Cin), .S(S[3:0]), .Cout(ripplecarryadder4bit_1_cout));
  RippleCarryAdder4Bit ripplecarryadder4bit_2 (
    .A(A[7:4]), .B(B[7:4]), .Cin(ripplecarryadder4bit_1_cout), .S(S[7:4]), .Cout(ripplecarryadder4bit_2_cout));
  RippleCarryAdder4Bit ripplecarryadder4bit_3 (
    .A(A[11:8]), .B(B[11:8]), .Cin(ripplecarryadder4bit_2_cout), .S(S[11:8]),
    .Cout(ripplecarryadder4bit_3_cout));
  RippleCarryAdder4Bit ripplecarryadder4bit_4 (
    .A(A[15:12]), .B(B[15:12]), .Cin(ripplecarryadder4bit_3_cout), .S(S[15:12]), .Cout(Cout));
endmodule

module Intel74181 (
  input  Cin,
  input  M,
  input  A0,
  input  B0,
  input  A1,
  input  B1,
  input  A2,
  input  B2,
  input  A3,
  input  B3,
  input  S0,
  input  S1,
  input  S2,
  input  S3,
  input  F0,
  input  F1,
  input  AeqB,
  input  F2,
  input  F3,
  input  P,
  input  CinIS4,
  input  G
);

  wire and_2_out, and_5_out, and_6_out, and_8_out, and_10_out, and_13_out, and_14_out, and_16_out,
       and_17_out, and_20_out, and_22_out, and_24_out, and_26_out, and_27_out, and_28_out, and_29_out,
       nor_1_out, nor_2_out, nor_5_out, nor_8_out, nor_11_out, not_1_out, not_3_out, not_5_out, not_7_out,
       not_9_out;

  not not_1 (not_1_out, M);
  // NAND_Gate nand_1 has open pins: in0=Cin, in1=not_1_out, out=open
  // NOT_Gate not_2 has open pins: in=nor_2_out, out=open
  // AND_Gate and_1 is placed but not wired
  nor nor_1 (nor_1_out, A0, and_2_out);
  nor nor_2 (nor_2_out, nor_1_out, and_5_out);
  and and_2 (and_2_out, B0, S0);
  // AND_Gate and_3 is placed but not wired
  // AND_Gate and_4 is placed but not wired
  // NOR_Gate nor_3 is placed but not wired
  not not_3 (not_3_out, B0);
  and and_5 (and_5_out, S1, not_3_out);
  and and_6 (and_6_out, not_3_out, A0, S2);
  // NOT_Gate not_4 is placed but not wired
  // NOR_Gate nor_4 has open pins: in0=and_6_out, in1=and_8_out, out=open
  // AND_Gate and_7 is placed but not wired
  and and_8 (and_8_out, B0, A0, S3);
  nor nor_5 (nor_5_out, A1, and_10_out);
  // AND_Gate and_9 is placed but not wired
  and and_10 (and_10_out, B1, S0);
  // NOR_Gate nor_6 has open pins: in0=nor_5_out, in1=and_13_out, out=open
  // AND_Gate and_11 is placed but not wired
  // AND_Gate and_12 is placed but not wired
  not not_5 (not_5_out, B1);
  and and_13 (and_13_out, S1, not_5_out);
  // NOT_Gate not_6 is placed but not wired
  and and_14 (and_14_out, not_5_out, S2, A1);
  // NOR_Gate nor_7 has open pins: in0=and_14_out, in1=and_16_out, out=open
  // AND_Gate and_15 is placed but not wired
  and and_16 (and_16_out, B1, A1, S3);
  and and_17 (and_17_out, B2, S0);
  nor nor_8 (nor_8_out, A2, and_17_out);
  // NOR_Gate nor_9 has open pins: in0=nor_8_out, in1=and_20_out, out=open
  // AND_Gate and_18 is placed but not wired
  // AND_Gate and_19 is placed but not wired
  and and_20 (and_20_out, S1, not_7_out);
  // AND_Gate and_21 is placed but not wired
  not not_7 (not_7_out, B2);
  and and_22 (and_22_out, not_7_out, A2, S2);
  // AND_Gate and_23 is placed but not wired
  and and_24 (and_24_out, B2, A2, S3);
  // NOR_Gate nor_10 has open pins: in0=and_22_out, in1=and_24_out, out=open
  // NOT_Gate not_8 is placed but not wired
  // AND_Gate and_25 is placed but not wired
  nor nor_11 (nor_11_out, A3, and_26_out);
  // NOR_Gate nor_12 has open pins: in0=nor_11_out, in1=and_27_out, out=open
  and and_26 (and_26_out, B3, S0);
  and and_27 (and_27_out, S1, not_9_out);
  not not_9 (not_9_out, B3);
  and and_28 (and_28_out, not_9_out, S2);
  and and_29 (and_29_out, B3, A3, S3);
  // NOR_Gate nor_13 has open pins: in0=and_28_out, in1=and_29_out, out=open
endmodule

module ALU (
  input  [3:0] Control,
  input  Cin,
  input  [31:0] A,
  input  [31:0] B,
  output [31:0] S,
  output Cout
);

  wire ripplecarryadder32bit_1_cout, ripplecarrysubtractor32bit_1_cout;
  wire [31:0] and32_1_s, nand32_1_s, nor32_1_s, not32_1_s, or32_1_s, ripplecarryadder32bit_1_s,
       ripplecarrysubtractor32bit_1_s, xnor32_1_s, xor32_1_s;

  RippleCarryAdder32Bit ripplecarryadder32bit_1 (
    .Cin(Cin), .A(A), .B(B), .S(ripplecarryadder32bit_1_s), .Cout(ripplecarryadder32bit_1_cout));
  RippleCarrySubtractor32Bit ripplecarrysubtractor32bit_1 (
    .A(A), .B(B), .S(ripplecarrysubtractor32bit_1_s), .Cout(ripplecarrysubtractor32bit_1_cout));
  NOT32 not32_1 (.A(A), .S(not32_1_s));
  AND32 and32_1 (.A(A), .B(B), .S(and32_1_s));
  NAND32 nand32_1 (.A(A), .B(B), .S(nand32_1_s));
  OR32 or32_1 (.A(A), .B(B), .S(or32_1_s));
  NOR32 nor32_1 (.A(A), .B(B), .S(nor32_1_s));
  XOR32 xor32_1 (.A(A), .B(B), .S(xor32_1_s));
  XNOR32 xnor32_1 (.A(A), .B(B), .S(xnor32_1_s));
  Multiplexer #(.select(4), .width(32)) multiplexer_1 (
    .in0(ripplecarryadder32bit_1_s), .in1(ripplecarrysubtractor32bit_1_s), .in2(not32_1_s), .in3(and32_1_s),
    .in4(nand32_1_s), .in5(or32_1_s), .in6(nor32_1_s), .in7(xor32_1_s), .in8(xnor32_1_s), .out(S),
    .sel(Control));  // open: in9, in10, in11, in12, in13, in14, in15
  Multiplexer #(.select(4)) multiplexer_2 (
    .in0(ripplecarryadder32bit_1_cout), .in1(ripplecarrysubtractor32bit_1_cout), .out(Cout), .sel(Control));  // open: in2, in3, in4, in5, in6, in7, in8, in9, in10, in11, in12, in13, in14, in15
endmodule

module NOT32 (
  input  [31:0] A,
  output [31:0] S
);

  not not_1 (S[31], A[31]);
  not not_2 (S[29], A[29]);
  not not_3 (S[27], A[27]);
  not not_4 (S[25], A[25]);
  not not_5 (S[30], A[30]);
  not not_6 (S[28], A[28]);
  not not_7 (S[26], A[26]);
  not not_8 (S[24], A[24]);
  not not_9 (S[23], A[23]);
  not not_10 (S[21], A[21]);
  not not_11 (S[19], A[19]);
  not not_12 (S[17], A[17]);
  not not_13 (S[22], A[22]);
  not not_14 (S[20], A[20]);
  not not_15 (S[18], A[18]);
  not not_16 (S[16], A[16]);
  not not_17 (S[15], A[15]);
  not not_18 (S[13], A[13]);
  not not_19 (S[11], A[11]);
  not not_20 (S[9], A[9]);
  not not_21 (S[14], A[14]);
  not not_22 (S[12], A[12]);
  not not_23 (S[10], A[10]);
  not not_24 (S[8], A[8]);
  not not_25 (S[7], A[7]);
  not not_26 (S[5], A[5]);
  not not_27 (S[3], A[3]);
  not not_28 (S[1], A[1]);
  not not_29 (S[6], A[6]);
  not not_30 (S[4], A[4]);
  not not_31 (S[2], A[2]);
  not not_32 (S[0], A[0]);
endmodule

module RippleCarrySubtractor32Bit (
  input  [31:0] A,
  input  [31:0] B,
  output [31:0] S,
  output Cout
);

  wire [31:0] not32_1_s;

  NOT32 not32_1 (.A(A), .S(not32_1_s));
  RippleCarryAdder32Bit ripplecarryadder32bit_1 (.Cin(1'b1), .A(not32_1_s), .B(B), .S(S), .Cout(Cout));
endmodule

module AND32 (
  input  [31:0] A,
  input  [31:0] B,
  output [31:0] S
);

  and and_1 (S[31], B[31], A[31]);
  and and_2 (S[30], B[30], A[30]);
  and and_3 (S[29], B[29], A[29]);
  and and_4 (S[28], B[28], A[28]);
  and and_5 (S[27], B[27], A[27]);
  and and_6 (S[26], B[26], A[26]);
  and and_7 (S[25], B[25], A[25]);
  and and_8 (S[24], B[24], A[24]);
  and and_9 (S[23], B[23], A[23]);
  and and_10 (S[22], B[22], A[22]);
  and and_11 (S[21], B[21], A[21]);
  and and_12 (S[20], B[20], A[20]);
  and and_13 (S[19], B[19], A[19]);
  and and_14 (S[18], B[18], A[18]);
  and and_15 (S[17], B[17], A[17]);
  and and_16 (S[15], B[15], A[15]);
  and and_17 (S[16], B[16], A[16]);
  and and_18 (S[14], B[14], A[14]);
  and and_19 (S[13], B[13], A[13]);
  and and_20 (S[12], B[12], A[12]);
  and and_21 (S[11], B[11], A[11]);
  and and_22 (S[10], B[10], A[10]);
  and and_23 (S[9], B[9], A[9]);
  and and_24 (S[8], B[8], A[8]);
  and and_25 (S[7], B[7], A[7]);
  and and_26 (S[6], B[6], A[6]);
  and and_27 (S[5], B[5], A[5]);
  and and_28 (S[4], B[4], A[4]);
  and and_29 (S[3], B[3], A[3]);
  and and_30 (S[2], B[2], A[2]);
  and and_31 (S[1], B[1], A[1]);
  and and_32 (S[0], B[0], A[0]);
endmodule

module OR32 (
  input  [31:0] A,
  input  [31:0] B,
  output [31:0] S
);

  or or_1 (S[31], B[31], A[31]);
  or or_2 (S[30], B[30], A[30]);
  or or_3 (S[29], B[29], A[29]);
  or or_4 (S[28], B[28], A[28]);
  or or_5 (S[27], B[27], A[27]);
  or or_6 (S[26], B[26], A[26]);
  or or_7 (S[25], B[25], A[25]);
  or or_8 (S[24], B[24], A[24]);
  or or_9 (S[23], B[23], A[23]);
  or or_10 (S[22], B[22], A[22]);
  or or_11 (S[21], B[21], A[21]);
  or or_12 (S[20], B[20], A[20]);
  or or_13 (S[19], B[19], A[19]);
  or or_14 (S[18], B[18], A[18]);
  or or_15 (S[17], B[17], A[17]);
  or or_16 (S[15], B[15], A[15]);
  or or_17 (S[16], B[16], A[16]);
  or or_18 (S[14], B[14], A[14]);
  or or_19 (S[13], B[13], A[13]);
  or or_20 (S[12], B[12], A[12]);
  or or_21 (S[11], B[11], A[11]);
  or or_22 (S[10], B[10], A[10]);
  or or_23 (S[9], B[9], A[9]);
  or or_24 (S[8], B[8], A[8]);
  or or_25 (S[7], B[7], A[7]);
  or or_26 (S[6], B[6], A[6]);
  or or_27 (S[5], B[5], A[5]);
  or or_28 (S[4], B[4], A[4]);
  or or_29 (S[3], B[3], A[3]);
  or or_30 (S[2], B[2], A[2]);
  or or_31 (S[1], B[1], A[1]);
  or or_32 (S[0], B[0], A[0]);
endmodule

module XOR32 (
  input  [31:0] A,
  input  [31:0] B,
  output [31:0] S
);

  xor xor_1 (S[31], B[31], A[31]);
  xor xor_2 (S[30], B[30], A[30]);
  xor xor_3 (S[29], B[29], A[29]);
  xor xor_4 (S[28], B[28], A[28]);
  xor xor_5 (S[27], B[27], A[27]);
  xor xor_6 (S[26], B[26], A[26]);
  xor xor_7 (S[25], B[25], A[25]);
  xor xor_8 (S[24], B[24], A[24]);
  xor xor_9 (S[23], B[23], A[23]);
  xor xor_10 (S[22], B[22], A[22]);
  xor xor_11 (S[21], B[21], A[21]);
  xor xor_12 (S[20], B[20], A[20]);
  xor xor_13 (S[19], B[19], A[19]);
  xor xor_14 (S[18], B[18], A[18]);
  xor xor_15 (S[17], B[17], A[17]);
  xor xor_16 (S[15], B[15], A[15]);
  xor xor_17 (S[16], B[16], A[16]);
  xor xor_18 (S[14], B[14], A[14]);
  xor xor_19 (S[13], B[13], A[13]);
  xor xor_20 (S[12], B[12], A[12]);
  xor xor_21 (S[11], B[11], A[11]);
  xor xor_22 (S[10], B[10], A[10]);
  xor xor_23 (S[9], B[9], A[9]);
  xor xor_24 (S[8], B[8], A[8]);
  xor xor_25 (S[7], B[7], A[7]);
  xor xor_26 (S[6], B[6], A[6]);
  xor xor_27 (S[5], B[5], A[5]);
  xor xor_28 (S[4], B[4], A[4]);
  xor xor_29 (S[3], B[3], A[3]);
  xor xor_30 (S[2], B[2], A[2]);
  xor xor_31 (S[1], B[1], A[1]);
  xor xor_32 (S[0], B[0], A[0]);
endmodule

module XNOR32 (
  input  [31:0] A,
  input  [31:0] B,
  output [31:0] S
);

  wire xor_1_out, xor_2_out, xor_3_out, xor_4_out, xor_5_out, xor_6_out, xor_7_out, xor_8_out, xor_9_out,
       xor_10_out, xor_11_out, xor_12_out, xor_13_out, xor_14_out, xor_15_out, xor_16_out, xor_17_out,
       xor_18_out, xor_19_out, xor_20_out, xor_21_out, xor_22_out, xor_23_out, xor_24_out, xor_25_out,
       xor_26_out, xor_27_out, xor_28_out, xor_29_out, xor_30_out, xor_31_out, xor_32_out;

  xor xor_1 (xor_1_out, B[31], A[31]);
  not not_1 (S[31], xor_1_out);
  xor xor_2 (xor_2_out, B[30], A[30]);
  not not_2 (S[30], xor_2_out);
  xor xor_3 (xor_3_out, B[29], A[29]);
  xor xor_4 (xor_4_out, B[28], A[28]);
  not not_3 (S[29], xor_3_out);
  not not_4 (S[28], xor_4_out);
  xor xor_5 (xor_5_out, B[27], A[27]);
  not not_5 (S[27], xor_5_out);
  xor xor_6 (xor_6_out, B[26], A[26]);
  xor xor_7 (xor_7_out, B[25], A[25]);
  not not_6 (S[26], xor_6_out);
  not not_7 (S[25], xor_7_out);
  xor xor_8 (xor_8_out, B[24], A[24]);
  xor xor_9 (xor_9_out, B[23], A[23]);
  not not_8 (S[24], xor_8_out);
  not not_9 (S[23], xor_9_out);
  xor xor_10 (xor_10_out, B[22], A[22]);
  not not_10 (S[22], xor_10_out);
  xor xor_11 (xor_11_out, B[21], A[21]);
  xor xor_12 (xor_12_out, B[20], A[20]);
  not not_11 (S[21], xor_11_out);
  not not_12 (S[20], xor_12_out);
  xor xor_13 (xor_13_out, B[19], A[19]);
  not not_13 (S[19], xor_13_out);
  xor xor_14 (xor_14_out, B[18], A[18]);
  xor xor_15 (xor_15_out, B[17], A[17]);
  not not_14 (S[18], xor_14_out);
  not not_15 (S[17], xor_15_out);
  xor xor_16 (xor_16_out, B[15], A[15]);
  xor xor_17 (xor_17_out, B[16], A[16]);
  not not_16 (S[15], xor_16_out);
  not not_17 (S[16], xor_17_out);
  xor xor_18 (xor_18_out, B[14], A[14]);
  not not_18 (S[14], xor_18_out);
  xor xor_19 (xor_19_out, B[13], A[13]);
  xor xor_20 (xor_20_out, B[12], A[12]);
  not not_19 (S[13], xor_19_out);
  not not_20 (S[12], xor_20_out);
  xor xor_21 (xor_21_out, B[11], A[11]);
  not not_21 (S[11], xor_21_out);
  xor xor_22 (xor_22_out, B[10], A[10]);
  xor xor_23 (xor_23_out, B[9], A[9]);
  not not_22 (S[10], xor_22_out);
  not not_23 (S[9], xor_23_out);
  xor xor_24 (xor_24_out, B[8], A[8]);
  xor xor_25 (xor_25_out, B[7], A[7]);
  not not_24 (S[8], xor_24_out);
  not not_25 (S[7], xor_25_out);
  xor xor_26 (xor_26_out, B[6], A[6]);
  not not_26 (S[6], xor_26_out);
  xor xor_27 (xor_27_out, B[5], A[5]);
  xor xor_28 (xor_28_out, B[4], A[4]);
  not not_27 (S[5], xor_27_out);
  not not_28 (S[4], xor_28_out);
  xor xor_29 (xor_29_out, B[3], A[3]);
  not not_29 (S[3], xor_29_out);
  xor xor_30 (xor_30_out, B[2], A[2]);
  xor xor_31 (xor_31_out, B[1], A[1]);
  not not_30 (S[2], xor_30_out);
  not not_31 (S[1], xor_31_out);
  xor xor_32 (xor_32_out, B[0], A[0]);
  not not_32 (S[0], xor_32_out);
endmodule

module NAND32 (
  input  [31:0] A,
  input  [31:0] B,
  output [31:0] S
);

  wire [31:0] and32_1_s;

  AND32 and32_1 (.A(A), .B(B), .S(and32_1_s));
  NOT32 not32_1 (.A(and32_1_s), .S(S));
endmodule

module NOR32 (
  input  [31:0] A,
  input  [31:0] B,
  output [31:0] S
);

  wire [31:0] or32_1_s;

  OR32 or32_1 (.A(A), .B(B), .S(or32_1_s));
  NOT32 not32_1 (.A(or32_1_s), .S(S));
endmodule

module CPU (
  input  in_1,
  output InvalidState
);

  wire undriven, undriven_2;
  wire [31:0] multiplexer_1_out, PC_s;

  Clock clock_1 ();  // open: out
  Multiplexer #(.width(32)) multiplexer_1 (.in0(PC_s), .out(multiplexer_1_out), .sel(undriven));  // open: in1
  // Probe on PC_s
  Memory4Bytes PC (.Clock(undriven_2), .Value(multiplexer_1_out), .S(PC_s));
  RegisterFile registerfile_1 ();  // open: Write, Clock, R, V, out_5
  ALU alu_1 ();  // open: Control, Cin, A, B, S, Cout
endmodule

module Memory4Bytes (
  input  Clock,
  input  [31:0] Value,
  output [31:0] S
);

  // Probe on S[7:0]
  Memory1Byte memory1byte_1 (.Clock(Clock), .Byte(Value[7:0]), .S(S[7:0]));
  // Probe on S[15:8]
  Memory1Byte memory1byte_2 (.Clock(Clock), .Byte(Value[15:8]), .S(S[15:8]));
  // Probe on S[23:16]
  Memory1Byte memory1byte_3 (.Clock(Clock), .Byte(Value[23:16]), .S(S[23:16]));
  // Probe on S[31:24]
  Memory1Byte memory1byte_4 (.Clock(Clock), .Byte(Value[31:24]), .S(S[31:24]));
endmodule

module Memory1Byte (
  input  Clock,
  input  [7:0] Byte,
  output [7:0] S
);

  D_Flip_Flop d_ff_1 (.D(Byte[0]), .clk(Clock), .Q(S[0]));  // open: Qn, preset, reset
  D_Flip_Flop d_ff_2 (.D(Byte[1]), .clk(Clock), .Q(S[1]));  // open: Qn, preset, reset
  D_Flip_Flop d_ff_3 (.D(Byte[2]), .clk(Clock), .Q(S[2]));  // open: Qn, preset, reset
  D_Flip_Flop d_ff_4 (.D(Byte[3]), .clk(Clock), .Q(S[3]));  // open: Qn, preset, reset
  D_Flip_Flop d_ff_5 (.D(Byte[4]), .clk(Clock), .Q(S[4]));  // open: Qn, preset, reset
  D_Flip_Flop d_ff_6 (.D(Byte[5]), .clk(Clock), .Q(S[5]));  // open: Qn, preset, reset
  D_Flip_Flop d_ff_7 (.D(Byte[6]), .clk(Clock), .Q(S[6]));  // open: Qn, preset, reset
  D_Flip_Flop d_ff_8 (.D(Byte[7]), .clk(Clock), .Q(S[7]));  // open: Qn, preset, reset
endmodule

module RegisterFile (
  input  Write,
  input  Clock,
  input  [3:0] R,
  input  [31:0] V,
  output [31:0] out_5
);

  wire demultiplexer_1_out0, demultiplexer_1_out1, demultiplexer_1_out2, demultiplexer_1_out3,
       demultiplexer_1_out4, demultiplexer_1_out5, demultiplexer_1_out6, demultiplexer_1_out7,
       demultiplexer_1_out8, demultiplexer_1_out9, demultiplexer_1_out10, demultiplexer_1_out11,
       demultiplexer_1_out12, demultiplexer_1_out13, demultiplexer_1_out14, demultiplexer_1_out15;
  wire [31:0] A_s, B_s, BP_s, C_s, D_s, demultiplexer_2_out0, demultiplexer_2_out1, demultiplexer_2_out2,
       demultiplexer_2_out3, demultiplexer_2_out4, demultiplexer_2_out5, demultiplexer_2_out6,
       demultiplexer_2_out7, demultiplexer_2_out8, demultiplexer_2_out9, demultiplexer_2_out10,
       demultiplexer_2_out11, demultiplexer_2_out12, demultiplexer_2_out13, demultiplexer_2_out14,
       demultiplexer_2_out15, E_s, F_s, FL_s, G_s, H_s, I_s, J_s, K_s, L_s, M_s, multiplexer_1_out,
       multiplexer_2_out, multiplexer_3_out, multiplexer_4_out, multiplexer_5_out, multiplexer_6_out,
       multiplexer_7_out, multiplexer_8_out, multiplexer_9_out, multiplexer_10_out, multiplexer_11_out,
       multiplexer_12_out, multiplexer_13_out, multiplexer_14_out, multiplexer_15_out, multiplexer_16_out,
       SP_s;

  Demultiplexer #(.select(4)) demultiplexer_1 (
    .out0(demultiplexer_1_out0), .out1(demultiplexer_1_out1), .out2(demultiplexer_1_out2),
    .out3(demultiplexer_1_out3), .out4(demultiplexer_1_out4), .out5(demultiplexer_1_out5),
    .out6(demultiplexer_1_out6), .out7(demultiplexer_1_out7), .out8(demultiplexer_1_out8),
    .out9(demultiplexer_1_out9), .out10(demultiplexer_1_out10), .out11(demultiplexer_1_out11),
    .out12(demultiplexer_1_out12), .out13(demultiplexer_1_out13), .out14(demultiplexer_1_out14),
    .out15(demultiplexer_1_out15), .in(Write), .sel(R));
  Demultiplexer #(.select(4), .width(32)) demultiplexer_2 (
    .out0(demultiplexer_2_out0), .out1(demultiplexer_2_out1), .out2(demultiplexer_2_out2),
    .out3(demultiplexer_2_out3), .out4(demultiplexer_2_out4), .out5(demultiplexer_2_out5),
    .out6(demultiplexer_2_out6), .out7(demultiplexer_2_out7), .out8(demultiplexer_2_out8),
    .out9(demultiplexer_2_out9), .out10(demultiplexer_2_out10), .out11(demultiplexer_2_out11),
    .out12(demultiplexer_2_out12), .out13(demultiplexer_2_out13), .out14(demultiplexer_2_out14),
    .out15(demultiplexer_2_out15), .in(V), .sel(R));
  Multiplexer #(.width(32)) multiplexer_1 (
    .in0(A_s), .in1(demultiplexer_2_out0), .out(multiplexer_1_out), .sel(demultiplexer_1_out0));
  Multiplexer #(.width(32)) multiplexer_2 (
    .in0(B_s), .in1(demultiplexer_2_out1), .out(multiplexer_2_out), .sel(demultiplexer_1_out1));
  Multiplexer #(.width(32)) multiplexer_3 (
    .in0(C_s), .in1(demultiplexer_2_out2), .out(multiplexer_3_out), .sel(demultiplexer_1_out2));
  Multiplexer #(.width(32)) multiplexer_4 (
    .in0(D_s), .in1(demultiplexer_2_out3), .out(multiplexer_4_out), .sel(demultiplexer_1_out3));
  Multiplexer #(.width(32)) multiplexer_5 (
    .in0(E_s), .in1(demultiplexer_2_out4), .out(multiplexer_5_out), .sel(demultiplexer_1_out4));
  Multiplexer #(.width(32)) multiplexer_6 (
    .in0(F_s), .in1(demultiplexer_2_out5), .out(multiplexer_6_out), .sel(demultiplexer_1_out5));
  Multiplexer #(.width(32)) multiplexer_7 (
    .in0(G_s), .in1(demultiplexer_2_out6), .out(multiplexer_7_out), .sel(demultiplexer_1_out6));
  Multiplexer #(.width(32)) multiplexer_8 (
    .in0(H_s), .in1(demultiplexer_2_out7), .out(multiplexer_8_out), .sel(demultiplexer_1_out7));
  Multiplexer #(.width(32)) multiplexer_9 (
    .in0(I_s), .in1(demultiplexer_2_out8), .out(multiplexer_9_out), .sel(demultiplexer_1_out8));
  Multiplexer #(.width(32)) multiplexer_10 (
    .in0(J_s), .in1(demultiplexer_2_out9), .out(multiplexer_10_out), .sel(demultiplexer_1_out9));
  Multiplexer #(.width(32)) multiplexer_11 (
    .in0(K_s), .in1(demultiplexer_2_out10), .out(multiplexer_11_out), .sel(demultiplexer_1_out10));
  Multiplexer #(.width(32)) multiplexer_12 (
    .in0(L_s), .in1(demultiplexer_2_out11), .out(multiplexer_12_out), .sel(demultiplexer_1_out11));
  Multiplexer #(.width(32)) multiplexer_13 (
    .in0(M_s), .in1(demultiplexer_2_out12), .out(multiplexer_13_out), .sel(demultiplexer_1_out12));
  Multiplexer #(.width(32)) multiplexer_14 (
    .in0(SP_s), .in1(demultiplexer_2_out13), .out(multiplexer_14_out), .sel(demultiplexer_1_out13));
  Multiplexer #(.width(32)) multiplexer_15 (
    .in0(BP_s), .in1(demultiplexer_2_out14), .out(multiplexer_15_out), .sel(demultiplexer_1_out14));
  Multiplexer #(.width(32)) multiplexer_16 (
    .in0(FL_s), .in1(demultiplexer_2_out15), .out(multiplexer_16_out), .sel(demultiplexer_1_out15));
  // Probe on A_s
  Memory4Bytes A (.Clock(Clock), .Value(multiplexer_1_out), .S(A_s));
  // Probe on B_s
  Memory4Bytes B (.Clock(Clock), .Value(multiplexer_2_out), .S(B_s));
  // Probe on C_s
  Memory4Bytes C (.Clock(Clock), .Value(multiplexer_3_out), .S(C_s));
  // Probe on D_s
  Memory4Bytes D (.Clock(Clock), .Value(multiplexer_4_out), .S(D_s));
  // Probe on E_s
  Memory4Bytes E (.Clock(Clock), .Value(multiplexer_5_out), .S(E_s));
  // Probe on F_s
  Memory4Bytes F (.Clock(Clock), .Value(multiplexer_6_out), .S(F_s));
  // Probe on G_s
  Memory4Bytes G (.Clock(Clock), .Value(multiplexer_7_out), .S(G_s));
  // Probe on H_s
  Memory4Bytes H (.Clock(Clock), .Value(multiplexer_8_out), .S(H_s));
  // Probe on I_s
  Memory4Bytes I (.Clock(Clock), .Value(multiplexer_9_out), .S(I_s));
  // Probe on J_s
  Memory4Bytes J (.Clock(Clock), .Value(multiplexer_10_out), .S(J_s));
  // Probe on K_s
  Memory4Bytes K (.Clock(Clock), .Value(multiplexer_11_out), .S(K_s));
  // Probe on L_s
  Memory4Bytes L (.Clock(Clock), .Value(multiplexer_12_out), .S(L_s));
  // Probe on M_s
  Memory4Bytes M (.Clock(Clock), .Value(multiplexer_13_out), .S(M_s));
  // Probe on SP_s
  Memory4Bytes SP (.Clock(Clock), .Value(multiplexer_14_out), .S(SP_s));
  // Probe on BP_s
  Memory4Bytes BP (.Clock(Clock), .Value(multiplexer_15_out), .S(BP_s));
  // Probe on FL_s
  Memory4Bytes FL (.Clock(Clock), .Value(multiplexer_16_out), .S(FL_s));
  Multiplexer #(.select(4), .width(32)) multiplexer_17 (
    .in0(A_s), .in1(B_s), .in2(C_s), .in3(D_s), .in4(E_s), .in5(F_s), .in6(G_s), .in7(H_s), .in8(I_s),
    .in9(J_s), .in10(K_s), .in11(L_s), .in12(M_s), .in13(SP_s), .in14(BP_s), .in15(FL_s), .out(out_5), .sel(R));
  // Probe on out_5
endmodule

module Memory4096Bytes (
  input  Clock,
  input  Write,
  input  [9:0] Address,
  input  [31:0] Value,
  output [31:0] S
);

  wire demultiplexer_1_out0, demultiplexer_1_out1, demultiplexer_1_out2, demultiplexer_1_out3;
  wire [31:0] demultiplexer_2_out0, demultiplexer_2_out1, demultiplexer_2_out2, demultiplexer_2_out3,
       memory1024bytes_1_s, memory1024bytes_2_s, memory1024bytes_3_s, memory1024bytes_4_s;

  Demultiplexer #(.select(2)) demultiplexer_1 (
    .out0(demultiplexer_1_out0), .out1(demultiplexer_1_out1), .out2(demultiplexer_1_out2),
    .out3(demultiplexer_1_out3), .in(Write), .sel(Address[9:8]));
  // Probe on Address[9:8]
  Demultiplexer #(.select(2), .width(32)) demultiplexer_2 (
    .out0(demultiplexer_2_out0), .out1(demultiplexer_2_out1), .out2(demultiplexer_2_out2),
    .out3(demultiplexer_2_out3), .in(Value), .sel(Address[9:8]));
  // Probe on demultiplexer_2_out1
  // Probe on demultiplexer_2_out2
  // Probe on demultiplexer_2_out3
  // Probe on Address[7:0]
  // Probe on demultiplexer_2_out0
  // Probe on memory1024bytes_1_s
  Memory1024Bytes memory1024bytes_1 (
    .Clock(Clock), .Write(demultiplexer_1_out0), .Address(Address[7:0]), .Value(demultiplexer_2_out0),
    .S(memory1024bytes_1_s));
  // Probe on memory1024bytes_2_s
  Memory1024Bytes memory1024bytes_2 (
    .Clock(Clock), .Write(demultiplexer_1_out1), .Address(Address[7:0]), .Value(demultiplexer_2_out1),
    .S(memory1024bytes_2_s));
  // Probe on memory1024bytes_3_s
  Memory1024Bytes memory1024bytes_3 (
    .Clock(Clock), .Write(demultiplexer_1_out2), .Address(Address[7:0]), .Value(demultiplexer_2_out2),
    .S(memory1024bytes_3_s));
  // Probe on memory1024bytes_4_s
  Memory1024Bytes memory1024bytes_4 (
    .Clock(Clock), .Write(demultiplexer_1_out3), .Address(Address[7:0]), .Value(demultiplexer_2_out3),
    .S(memory1024bytes_4_s));
  // Probe on Address[9:8]
  Multiplexer #(.select(2), .width(32)) multiplexer_1 (
    .in0(memory1024bytes_1_s), .in1(memory1024bytes_2_s), .in2(memory1024bytes_3_s),
    .in3(memory1024bytes_4_s), .out(S), .sel(Address[9:8]));
endmodule

module Memory16Bytes (
  input  Clock,
  input  Write,
  input  [1:0] Address,
  input  [31:0] Value,
  output [31:0] S
);

  wire demultiplexer_1_out0, demultiplexer_1_out1, demultiplexer_1_out2, demultiplexer_1_out3;
  wire [31:0] demultiplexer_2_out0, demultiplexer_2_out1, demultiplexer_2_out2, demultiplexer_2_out3,
       memory4bytes_1_s, memory4bytes_2_s, memory4bytes_3_s, memory4bytes_4_s, multiplexer_1_out,
       multiplexer_2_out, multiplexer_3_out, multiplexer_4_out;

  Demultiplexer #(.select(2)) demultiplexer_1 (
    .out0(demultiplexer_1_out0), .out1(demultiplexer_1_out1), .out2(demultiplexer_1_out2),
    .out3(demultiplexer_1_out3), .in(Write), .sel(Address));
  Demultiplexer #(.select(2), .width(32)) demultiplexer_2 (
    .out0(demultiplexer_2_out0), .out1(demultiplexer_2_out1), .out2(demultiplexer_2_out2),
    .out3(demultiplexer_2_out3), .in(Value), .sel(Address));
  Multiplexer #(.width(32)) multiplexer_1 (
    .in0(memory4bytes_1_s), .in1(demultiplexer_2_out0), .out(multiplexer_1_out), .sel(demultiplexer_1_out0));
  Multiplexer #(.width(32)) multiplexer_2 (
    .in0(memory4bytes_2_s), .in1(demultiplexer_2_out1), .out(multiplexer_2_out), .sel(demultiplexer_1_out1));
  Multiplexer #(.width(32)) multiplexer_3 (
    .in0(memory4bytes_3_s), .in1(demultiplexer_2_out2), .out(multiplexer_3_out), .sel(demultiplexer_1_out2));
  Multiplexer #(.width(32)) multiplexer_4 (
    .in0(memory4bytes_4_s), .in1(demultiplexer_2_out3), .out(multiplexer_4_out), .sel(demultiplexer_1_out3));
  // Probe on memory4bytes_1_s
  Memory4Bytes memory4bytes_1 (.Clock(Clock), .Value(multiplexer_1_out), .S(memory4bytes_1_s));
  // Probe on memory4bytes_2_s
  Memory4Bytes memory4bytes_2 (.Clock(Clock), .Value(multiplexer_2_out), .S(memory4bytes_2_s));
  // Probe on memory4bytes_3_s
  Memory4Bytes memory4bytes_3 (.Clock(Clock), .Value(multiplexer_3_out), .S(memory4bytes_3_s));
  // Probe on memory4bytes_4_s
  Memory4Bytes memory4bytes_4 (.Clock(Clock), .Value(multiplexer_4_out), .S(memory4bytes_4_s));
  Multiplexer #(.select(2), .width(32)) multiplexer_5 (
    .in0(memory4bytes_1_s), .in1(memory4bytes_2_s), .in2(memory4bytes_3_s), .in3(memory4bytes_4_s), .out(S),
    .sel(Address));
endmodule

module Memory64Bytes (
  input  Clock,
  input  Write,
  input  [3:0] Address,
  input  [31:0] Value,
  output [31:0] S
);

  wire demultiplexer_1_out0, demultiplexer_1_out1, demultiplexer_1_out2, demultiplexer_1_out3;
  wire [31:0] demultiplexer_2_out0, demultiplexer_2_out1, demultiplexer_2_out2, demultiplexer_2_out3,
       memory16bytes_1_s, memory16bytes_2_s, memory16bytes_3_s, memory16bytes_4_s;

  Demultiplexer #(.select(2)) demultiplexer_1 (
    .out0(demultiplexer_1_out0), .out1(demultiplexer_1_out1), .out2(demultiplexer_1_out2),
    .out3(demultiplexer_1_out3), .in(Write), .sel(Address[3:2]));
  Demultiplexer #(.select(2), .width(32)) demultiplexer_2 (
    .out0(demultiplexer_2_out0), .out1(demultiplexer_2_out1), .out2(demultiplexer_2_out2),
    .out3(demultiplexer_2_out3), .in(Value), .sel(Address[3:2]));
  // Probe on Address[3:2]
  // Probe on memory16bytes_1_s
  Memory16Bytes memory16bytes_1 (
    .Clock(Clock), .Write(demultiplexer_1_out0), .Address(Address[1:0]), .Value(demultiplexer_2_out0),
    .S(memory16bytes_1_s));
  // Probe on memory16bytes_2_s
  Memory16Bytes memory16bytes_2 (
    .Clock(Clock), .Write(demultiplexer_1_out1), .Address(Address[1:0]), .Value(demultiplexer_2_out1),
    .S(memory16bytes_2_s));
  // Probe on memory16bytes_3_s
  Memory16Bytes memory16bytes_3 (
    .Clock(Clock), .Write(demultiplexer_1_out2), .Address(Address[1:0]), .Value(demultiplexer_2_out2),
    .S(memory16bytes_3_s));
  // Probe on memory16bytes_4_s
  Memory16Bytes memory16bytes_4 (
    .Clock(Clock), .Write(demultiplexer_1_out3), .Address(Address[1:0]), .Value(demultiplexer_2_out3),
    .S(memory16bytes_4_s));
  // Probe on Address[3:2]
  Multiplexer #(.select(2), .width(32)) multiplexer_1 (
    .in0(memory16bytes_1_s), .in1(memory16bytes_2_s), .in2(memory16bytes_3_s), .in3(memory16bytes_4_s),
    .out(S), .sel(Address[3:2]));
endmodule

module Memory1024Bytes (
  input  Clock,
  input  Write,
  input  [7:0] Address,
  input  [31:0] Value,
  output [31:0] S
);

  wire demultiplexer_1_out0, demultiplexer_1_out1, demultiplexer_1_out2, demultiplexer_1_out3;
  wire [31:0] demultiplexer_2_out0, demultiplexer_2_out1, demultiplexer_2_out2, demultiplexer_2_out3,
       memory256bytes_1_s, memory256bytes_2_s, memory256bytes_3_s, memory256bytes_4_s;

  Demultiplexer #(.select(2)) demultiplexer_1 (
    .out0(demultiplexer_1_out0), .out1(demultiplexer_1_out1), .out2(demultiplexer_1_out2),
    .out3(demultiplexer_1_out3), .in(Write), .sel(Address[7:6]));
  // Probe on Address[7:6]
  Demultiplexer #(.select(2), .width(32)) demultiplexer_2 (
    .out0(demultiplexer_2_out0), .out1(demultiplexer_2_out1), .out2(demultiplexer_2_out2),
    .out3(demultiplexer_2_out3), .in(Value), .sel(Address[7:6]));
  // Probe on demultiplexer_2_out1
  // Probe on demultiplexer_2_out2
  // Probe on demultiplexer_2_out3
  // Probe on Address[5:0]
  // Probe on demultiplexer_2_out0
  // Probe on memory256bytes_1_s
  Memory256Bytes memory256bytes_1 (
    .Clock(Clock), .Write(demultiplexer_1_out0), .Address(Address[5:0]), .Value(demultiplexer_2_out0),
    .S(memory256bytes_1_s));
  // Probe on memory256bytes_2_s
  Memory256Bytes memory256bytes_2 (
    .Clock(Clock), .Write(demultiplexer_1_out1), .Address(Address[5:0]), .Value(demultiplexer_2_out1),
    .S(memory256bytes_2_s));
  // Probe on memory256bytes_3_s
  Memory256Bytes memory256bytes_3 (
    .Clock(Clock), .Write(demultiplexer_1_out2), .Address(Address[5:0]), .Value(demultiplexer_2_out2),
    .S(memory256bytes_3_s));
  // Probe on memory256bytes_4_s
  Memory256Bytes memory256bytes_4 (
    .Clock(Clock), .Write(demultiplexer_1_out3), .Address(Address[5:0]), .Value(demultiplexer_2_out3),
    .S(memory256bytes_4_s));
  // Probe on Address[7:6]
  Multiplexer #(.select(2), .width(32)) multiplexer_1 (
    .in0(memory256bytes_1_s), .in1(memory256bytes_2_s), .in2(memory256bytes_3_s), .in3(memory256bytes_4_s),
    .out(S), .sel(Address[7:6]));
endmodule

module Accumulator4 (
  input  Clock,
  output [1:0] S
);

  wire and_1_out, and_2_out, not_1_out, not_2_out, not_3_out;

  and and_1 (and_1_out, not_1_out, 1'b1);
  D_Flip_Flop d_ff_1 (.D(and_1_out), .clk(Clock), .Q(S[0]));  // open: Qn, preset, reset
  D_Flip_Flop d_ff_2 (.D(and_2_out), .clk(not_2_out), .Q(S[1]));  // open: Qn, preset, reset
  buf and_2 (and_2_out, not_3_out);  // AND_Gate
  not not_1 (not_1_out, S[0]);
  not not_2 (not_2_out, S[0]);
  not not_3 (not_3_out, S[1]);
endmodule

module Memory256Bytes (
  input  Clock,
  input  Write,
  input  [5:0] Address,
  input  [31:0] Value,
  output [31:0] S
);

  wire demultiplexer_1_out0, demultiplexer_1_out1, demultiplexer_1_out2, demultiplexer_1_out3;
  wire [31:0] demultiplexer_2_out0, demultiplexer_2_out1, demultiplexer_2_out2, demultiplexer_2_out3,
       memory64bytes_1_s, memory64bytes_2_s, memory64bytes_3_s, memory64bytes_4_s;

  Demultiplexer #(.select(2)) demultiplexer_1 (
    .out0(demultiplexer_1_out0), .out1(demultiplexer_1_out1), .out2(demultiplexer_1_out2),
    .out3(demultiplexer_1_out3), .in(Write), .sel(Address[5:4]));
  // Probe on Address[5:4]
  Demultiplexer #(.select(2), .width(32)) demultiplexer_2 (
    .out0(demultiplexer_2_out0), .out1(demultiplexer_2_out1), .out2(demultiplexer_2_out2),
    .out3(demultiplexer_2_out3), .in(Value), .sel(Address[5:4]));
  // Probe on demultiplexer_2_out1
  // Probe on demultiplexer_2_out2
  // Probe on demultiplexer_2_out3
  // Probe on Address[3:0]
  // Probe on demultiplexer_2_out0
  // Probe on memory64bytes_1_s
  Memory64Bytes memory64bytes_1 (
    .Clock(Clock), .Write(demultiplexer_1_out0), .Address(Address[3:0]), .Value(demultiplexer_2_out0),
    .S(memory64bytes_1_s));
  // Probe on memory64bytes_2_s
  Memory64Bytes memory64bytes_2 (
    .Clock(Clock), .Write(demultiplexer_1_out1), .Address(Address[3:0]), .Value(demultiplexer_2_out1),
    .S(memory64bytes_2_s));
  // Probe on memory64bytes_3_s
  Memory64Bytes memory64bytes_3 (
    .Clock(Clock), .Write(demultiplexer_1_out2), .Address(Address[3:0]), .Value(demultiplexer_2_out2),
    .S(memory64bytes_3_s));
  // Probe on memory64bytes_4_s
  Memory64Bytes memory64bytes_4 (
    .Clock(Clock), .Write(demultiplexer_1_out3), .Address(Address[3:0]), .Value(demultiplexer_2_out3),
    .S(memory64bytes_4_s));
  // Probe on Address[5:4]
  Multiplexer #(.select(2), .width(32)) multiplexer_1 (
    .in0(memory64bytes_1_s), .in1(memory64bytes_2_s), .in2(memory64bytes_3_s), .in3(memory64bytes_4_s),
    .out(S), .sel(Address[5:4]));
endmodule
